# Fritzing sketch lcd (saved by Fritzing 1.0.3b)
breadboards: 3

parts:
  U1 = LCD-16X2 [package=lcd-16x2]
  S1 = Momentary Switch [package=ksa_sealed_tac_switch]
  S2 = Momentary Switch [package=ksa_sealed_tac_switch]
  S3 = Momentary Switch [package=ksa_sealed_tac_switch]
  R1 = Resistor [tolerance=±5% resistance=220 package="2512 [SMD]"]
  R2 = Resistor [tolerance=±5% resistance=220 package="2512 [SMD]"]
  R3 = Resistor [tolerance=±5% resistance=220 package="2512 [SMD]"]
  LED1 = smd LED [color="Red (633nm)" package="1206 [SMD]"]
  LED2 = smd LED [color="Green (555nm)" package="1206 [SMD]"]
  LED3 = smd LED [color="Blue (430nm)" package="1206 [SMD]"]
  R4 = Resistor [tolerance=±5% resistance=220 package="2512 [SMD]"]
  R5 = Resistor [tolerance=±5% resistance=220 package="2512 [SMD]"]
  R6 = Resistor [tolerance=±5% resistance=220 package="2512 [SMD]"]
  A1 = Raspberry Pi Pico W
  R7 = Resistor [tolerance=±5% resistance=220 package="2512 [SMD]"]

nets:
  N1: U1.VSS, U1.R_W, U1.K, R1.Pin_1, R2.Pin_1, R3.Pin_1, LED1.cathode, LED2.cathode, LED3.cathode, A1.pin_3, A1.pin_8, A1.pin_13, A1.pin_18, A1.pin_23, A1.pin_28, A1.pin_33, A1.pin_38, R7.Pin_1
  N2: U1.VDD, U1.A, A1.pin_20
  N3: U1.VO, R7.Pin_0
  N4: U1.RS, A1.pin_40
  N5: U1.E, A1.pin_39
  N6: U1.DB4, A1.pin_36
  N7: U1.DB5, A1.pin_37
  N8: U1.DB6, A1.pin_1
  N9: U1.DB7, A1.pin_2
  N10: S1.2, R1.Pin_0, A1.pin_7
  N11: S1.3, S2.3, S3.3, A1.pin_15
  N12: S2.2, R2.Pin_0, A1.pin_9
  N13: S3.2, R3.Pin_0, A1.pin_22
  N14: LED1.anode, R4.Pin_0
  N15: LED2.anode, R5.Pin_0
  N16: LED3.anode, R6.Pin_0
  N17: R4.Pin_1, A1.pin_4
  N18: R5.Pin_1, A1.pin_5
  N19: R6.Pin_1, A1.pin_6

custom parts:
  Raspberry Pi Pico W: Raspberry Pi Pico W. Based around the RP2040 microcontroller the Pico W is a low cost microcontroller device bringing Raspberry Pi quality, cost, and easy of use to the microcontroller space. The areas marked KEEPOUT in pcb silkscreen should not have traces running through them to avoid shorts on a soldered in module!
